# Fritzing sketch ICT5101_CiruitDiagram (saved by Fritzing 1.0.2b)
breadboards: 1

parts:
  Part2 = Arduino Nano (Rev3.0)
  LED3 = RGB LED (com. cathode, rgb) [color="Red (633nm)" current=0.030A package="5 mm [THT]"]
  R1 = Resistor [tolerance=±5% resistance=220 package="0402 [SMD]"]
  R2 = Resistor [tolerance=±5% resistance=220 package="0402 [SMD]"]
  R3 = Resistor [tolerance=±5% resistance=220 package="0402 [SMD]"]
  OLED1 = OLED 128x64 I2C Monochrome Display GND-VDD
  Part3 = Soil Moisture Sensor

nets:
  GND: Part2.GND, LED3.common_cathode, OLED1.GND, Part3.GND
  N1: Part2.D2, R3.Pin_1
  N2: Part2.D3, R2.Pin_1
  N3: Part2.D4, R1.Pin_1
  5V: Part2.5V, OLED1.VDD, Part3.VCC
  N4: Part2.A5, OLED1.SCK
  N5: Part2.A4, OLED1.SDA
  N6: Part2.A3, Part3.SIG
  N7: LED3.red_anode, R3.Pin_0
  N8: LED3.green_anode, R2.Pin_0
  N9: LED3.blue_anode, R1.Pin_0

notes:
  Colour Key:
  - RGB LED
  - Orange - D2 - R
  - Green - D3 - G
  - Blue - D4 - B
  - OLED Monitor
  - White - A5 - SCL
  - Blue - A4 - SDA
  - Moisture Sensor
  - Purple - A3 - Sig
  Black - GND
  Red - 5V - VCC

custom parts:
  OLED 128x64 I2C Monochrome Display GND-VDD: OLED 128x64 I2C Monochrome Display. Note: there are two variants of this part, this one is the GND VDD SCK SDA variant. The other is VDD GND SCK SDA. Make sure you select the part that matches your module as using the incorrect part will probably destroy your module! In addition the mounting holes are marked on silkscreen but not by default drilled. If you want drilled mounting holes, copy a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
